// Logisim project LC-3.circ as structural Verilog: 18 circuits, main circuit main
module main (
  input  Reset,
  output out_2,
  output out_3,
  output out_4,
  output out_5,
  output out_6,
  output out_7,
  output out_8,
  output [15:0] out_9,
  output [15:0] out_10,
  output [15:0] out_11,
  output [15:0] out_12,
  output [15:0] out_13,
  output [15:0] out_14,
  output [15:0] out_15,
  output [15:0] out_16,
  output [15:0] out_17,
  output halt,
  output [15:0] out_19,
  output [15:0] out_20,
  output [15:0] out_21,
  output [15:0] out_22
);

  wire and_3_out, Arith, decodeir_1_writereg, DoubleIndirection, getcst_1_usecst, LoadAddUnit, LoadMem,
       or16_1_out_2, or16_2_out_2, Post_Exec, Post_Fetch, ramctrl_1_memload, ramctrl_1_memstore,
       UseCondition, WriteR7;
  wire [2:0] nzp_1_nzp;
  wire [15:0] alu_1_output, BaseR, getcst_1_cst, RegIN, registres_1_out_sr2, Result;

  BiClock biclock_1 (.reset(Reset), .fetch(out_2), .exec(out_3), .post_fetch(Post_Fetch), .post_exec(Post_Exec));
  RegPC regpc_1 (
    .H(out_3), .PC(out_9), .Reset(Reset), .Result(Result), .TestNZP(out_5), .Jump(out_4),
    .UseCondition(UseCondition));
  // Probe on out_9
  GetAddr getaddr_1 (
    .PC(out_9), .R(Result), .MemOUT(out_13), .Addr(out_11), .Post_Fetch(Post_Fetch),
    .DoubleIndirection(DoubleIndirection), .Exec(out_3));
  // Probe on out_11
  // Probe on out_12
  RAM #(.addrWidth(16), .dataWidth(16), .bus("separate")) ram_1 (
    .addr(out_11), .din(out_12), .data(out_13), .str(ramctrl_1_memstore), .clk(ramctrl_1_memstore),
    .ld(ramctrl_1_memload));  // open: sel, clr
  LED led_1 (.in(out_6));
  RamCtrl ramctrl_1 (
    .Store(out_7), .Fetch(out_2), .Exec(out_3), .Load(out_6), .MemStore(ramctrl_1_memstore),
    .MemLoad(ramctrl_1_memload), .DoubleIndirection(DoubleIndirection), .Post_Exec(Post_Exec),
    .Post_Fetch(Post_Fetch));
  LED led_2 (.in(out_7));
  AddUnit addunit_1 (.IR(out_10), .PC(out_9), .R(BaseR), .Out(Result));
  LED led_3 (.in(DoubleIndirection));
  DecodeIR decodeir_1 (
    .Opcode(out_10[15:12]), .Jump(out_4), .WriteReg(decodeir_1_writereg), .Load(out_6), .Store(out_7),
    .Arith(Arith), .LoadMem(LoadMem), .LoadAddUnit(LoadAddUnit), .WriteR7(WriteR7),
    .DoubleIndirection(DoubleIndirection), .UseCondition(UseCondition));
  // Probe on out_13
  // Probe on out_10[15:12]
  Register #(.width(16), .trigger("falling")) RegIR (.D(out_13), .Q(out_10), .clk(out_2));  // open: en, clr
  Or16 or16_1 (.in_1(out_10), .out_2(or16_1_out_2));
  Or16 or16_2 (.in_1(out_9), .out_2(or16_2_out_2));
  // Probe on out_10[11:9]
  // Probe on out_10[8:6]
  // Probe on out_10[2:0]
  // Probe on BaseR
  ALU alu_1 (
    .UseCst(getcst_1_usecst), .e2(out_10[15:14]), .Input1(BaseR), .Input2(registres_1_out_sr2),
    .Cst(getcst_1_cst), .Output(alu_1_output));
  // Probe on getcst_1_cst
  GetCst getcst_1 (.IR(out_10), .Cst(getcst_1_cst), .UseCst(getcst_1_usecst));
  // Probe on out_10[15:14]
  and and_1 (out_8, out_3, decodeir_1_writereg);
  and and_2 (halt, ~or16_1_out_2, or16_2_out_2);  // AND_Gate
  Registres registres_1 (
    .SR1(out_10[8:6]), .IN(RegIN), .SR2(out_10[2:0]), .WriteReg(out_8), .DR_SR(out_10[11:9]),
    .OUT_SR1(BaseR), .OUT_SR2(registres_1_out_sr2), .OUT_SR(out_12), .R0(out_14), .R1(out_15), .R2(out_16),
    .R3(out_17), .R4(out_19), .R5(out_20), .R6(out_21), .R7(out_22), .WriteR7(WriteR7));
  // Probe on registres_1_out_sr2
  // Probe on alu_1_output
  // Probe on out_14
  // Probe on out_15
  // Probe on out_16
  // Probe on out_17
  // Probe on out_19
  // Probe on out_20
  // Probe on out_21
  // Probe on out_22
  NZP nzp_1 (.RES(RegIN), .NZP(nzp_1_nzp), .IR(out_10), .TestNZP(out_5), .WriteReg(and_3_out));
  // Probe on nzp_1_nzp
  and and_3 (and_3_out, out_8, ~WriteR7);  // AND_Gate
  WriteSelector writeselector_1 (
    .MemOut(out_13), .AddUnitOut(Result), .PC(out_9), .ALUOut(alu_1_output), .LoadMem(LoadMem),
    .LoadAddUnit(LoadAddUnit), .WriteR7(WriteR7), .Arith(Arith), .Output(RegIN));

  // Other names for the same wires on the sheet: Addr[15:0] = out_11; Condition = out_5; Exec = out_3; Fetch = out_2;
  //   IR[15:0] = out_10; JumpInstr = out_4; Load = out_6; MemIN[15:0] = out_12; MemOUT[15:0] = out_13;
  //   PC[15:0] = out_9; R0[15:0] = out_14; R1[15:0] = out_15; R2[15:0] = out_16; R3[15:0] = out_17; R4[15:0] = out_19;
  //   R5[15:0] = out_20; R6[15:0] = out_21; R7[15:0] = out_22; Store = out_7; WriteReg = out_8

  // Notes on the sheet:
  //   Result
  //   Result
  //   MemOUT
  //   RAM
  //   Traces (NE PAS MODIFIER)______________________________________________________________________________________________________
  //   GetOp
  //   Arret des traces au 1er NOP
  //   GetRegs
endmodule

module ALU (
  input  [15:0] Input1,
  input  [15:0] Input2,
  input  [15:0] Cst,
  input  UseCst,
  input  [1:0] e2,
  output [15:0] Output
);

  wire [15:0] adder_1_out, and_1_out, multiplexer_1_out, not_1_out, setresetbit_1_dataout;

  Multiplexer #(.width(16), .enable("false")) multiplexer_1 (
    .in0(Input2), .in1(Cst), .out(multiplexer_1_out), .sel(UseCst));
  Adder #(.width(16)) adder_1 (.a(multiplexer_1_out), .b(Input1), .out(adder_1_out));  // open: cin, cout
  assign and_1_out = Input1 & multiplexer_1_out;  // AND_Gate and_1, 16 bits wide
  Multiplexer #(.select(2), .width(16), .enable("false")) multiplexer_2 (
    .in0(adder_1_out), .in1(and_1_out), .in2(not_1_out), .in3(setresetbit_1_dataout), .out(Output), .sel(e2));
  assign not_1_out = ~Input1;  // NOT_Gate not_1, 16 bits wide
  setResetBit setresetbit_1 (
    .DataIn(Input1), .NBit(multiplexer_1_out), .DataOut(setresetbit_1_dataout), .Mode__0__Reset_1__Set(Cst[4]));
endmodule

module BiClock (
  input  reset,
  output fetch,
  output post_fetch,
  output exec,
  output post_exec
);

  wire and_1_out, horloge_out, not_1_out, register_1_q;

  Clock horloge (.out(horloge_out));
  not not_1 (not_1_out, register_1_q);
  Register #(.width(1), .trigger("falling")) register_1 (
    .D(not_1_out), .Q(register_1_q), .clk(horloge_out), .clr(reset));  // open: en
  and and_1 (and_1_out, horloge_out, ~reset);  // AND_Gate
  and and_2 (fetch, ~register_1_q, and_1_out);  // AND_Gate
  and and_3 (post_fetch, register_1_q, ~and_1_out);  // AND_Gate
  and and_4 (exec, register_1_q, and_1_out);
  and and_5 (post_exec, ~register_1_q, ~and_1_out);  // AND_Gate

  // Notes on the sheet:
  //   Ce module divise une horloge en deux sous-horloges alternées
  //   Chronogrammes :
  //   horloge: 0101010101 signal0: 0100010001 signal1: 000100010
  //   registre 1-bit
  //   Enable
  //   select : 0 / 1
endmodule

module DecodeIR (
  input  [3:0] Opcode,
  output LoadMem,
  output LoadAddUnit,
  output WriteR7,
  output Arith,
  output WriteReg,
  output Jump,
  output UseCondition,
  output Load,
  output Store,
  output DoubleIndirection
);

  wire and_1_out, and_2_out, and_3_out, and_5_out, and_6_out, and_8_out, and_9_out, and_10_out, and_11_out,
       and_12_out, and_13_out, and_15_out, and_16_out, and_17_out, and_18_out, and_19_out;

  // Probe on Opcode[3]
  // Probe on Opcode[2]
  // Probe on Opcode[1]
  // Probe on Opcode[0]
  and and_1 (and_1_out, Opcode[0], Opcode[1]);
  and and_2 (and_2_out, Opcode[1], ~Opcode[3]);  // AND_Gate
  and and_3 (and_3_out, Opcode[1], ~Opcode[2]);  // AND_Gate
  and and_4 (LoadAddUnit, ~Opcode[0], Opcode[2], Opcode[3]);  // AND_Gate
  and and_5 (and_5_out, Opcode[0], Opcode[1], Opcode[2], Opcode[3]);
  and and_6 (and_6_out, ~Opcode[0], ~Opcode[1], Opcode[2], ~Opcode[3]);  // AND_Gate
  and and_7 (Arith, Opcode[0], ~Opcode[1]);  // AND_Gate
  and and_8 (and_8_out, Opcode[0], ~Opcode[1]);  // AND_Gate
  and and_9 (and_9_out, ~Opcode[0], Opcode[1]);  // AND_Gate
  and and_10 (and_10_out, Opcode[0], Opcode[2], Opcode[3]);
  and and_11 (and_11_out, ~Opcode[1], Opcode[2], ~Opcode[3]);  // AND_Gate
  and and_12 (and_12_out, ~Opcode[0], ~Opcode[1]);  // AND_Gate
  and and_13 (and_13_out, Opcode[0], Opcode[1], Opcode[2], Opcode[3]);
  and and_14 (UseCondition, ~Opcode[0], ~Opcode[1], ~Opcode[2], ~Opcode[3]);  // AND_Gate
  and and_15 (and_15_out, ~Opcode[0], Opcode[1], ~Opcode[3]);  // AND_Gate
  and and_16 (and_16_out, Opcode[0], Opcode[1], Opcode[2], Opcode[3]);
  and and_17 (and_17_out, Opcode[1], ~Opcode[2], Opcode[3]);  // AND_Gate
  and and_18 (and_18_out, Opcode[0], Opcode[1], ~Opcode[3]);  // AND_Gate
  and and_19 (and_19_out, Opcode[0], Opcode[1], ~Opcode[2], Opcode[3]);  // AND_Gate
  and and_20 (DoubleIndirection, Opcode[1], ~Opcode[2], Opcode[3]);  // AND_Gate
  or or_1 (LoadMem, and_1_out, and_2_out, and_3_out);
  or or_2 (WriteR7, and_5_out, and_6_out);
  or or_3 (WriteReg, and_8_out, and_9_out, and_10_out, and_11_out);
  or or_4 (Jump, and_12_out, and_13_out);
  or or_5 (Load, and_15_out, and_16_out, and_17_out);
  or or_6 (Store, and_18_out, and_19_out);
endmodule

module GetAddr (
  input  [15:0] PC,
  input  [15:0] MemOUT,
  input  [15:0] R,
  input  Exec,
  input  Post_Fetch,
  input  DoubleIndirection,
  output [15:0] Addr
);

  wire and_1_out, and_2_out, or_1_out;
  wire [15:0] addrIndirection_q, multiplexer_1_out;

  Register #(.width(16), .trigger("falling")) addrIndirection (
    .D(MemOUT), .Q(addrIndirection_q), .clk(and_1_out));  // open: en, clr
  and and_1 (and_1_out, Post_Fetch, DoubleIndirection);
  and and_2 (and_2_out, DoubleIndirection, Exec);
  or or_1 (or_1_out, Exec, Post_Fetch);
  Multiplexer #(.width(16), .enable("false")) multiplexer_1 (
    .in0(R), .in1(addrIndirection_q), .out(multiplexer_1_out), .sel(and_2_out));
  Multiplexer #(.width(16), .enable("false")) multiplexer_2 (
    .in0(PC), .in1(multiplexer_1_out), .out(Addr), .sel(or_1_out));

  // Notes on the sheet:
  //   Adresse Memoire
  //   (toujours PC pour l'instant)
endmodule

module GetCst (
  input  [15:0] IR,
  output [15:0] Cst,
  output UseCst
);

  assign Cst = {{11{IR[4]}}, IR[4:0]};  // Bit_Extender bit_extender_1

  assign UseCst = IR[5];
endmodule

module NZP (
  input  [15:0] RES,
  input  WriteReg,
  input  [15:0] IR,
  output [2:0] NZP,
  output TestNZP
);

  wire and_3_out, and_4_out, and_5_out, or16_1_out_2;
  wire [2:0] and_1_out;

  Or16 or16_1 (.in_1(RES), .out_2(or16_1_out_2));
  not not_1 (and_1_out[1], or16_1_out_2);
  and and_1 (and_1_out[0], ~RES[15], ~and_1_out[1]);  // AND_Gate
  and and_2 (and_1_out[2], ~and_1_out[1], RES[15]);  // AND_Gate
  // Probe on IR[10]
  // Probe on IR[11]
  Register #(.width(3), .trigger("falling")) u_NZP (.D(and_1_out), .Q(NZP), .clk(WriteReg));  // open: en, clr
  // Probe on NZP[1]
  // Probe on NZP[2]
  // Probe on IR[9]
  and and_3 (and_3_out, NZP[0], IR[9]);
  and and_4 (and_4_out, NZP[1], IR[10]);
  and and_5 (and_5_out, NZP[2], IR[11]);
  // Probe on NZP[0]
  or or_1 (TestNZP, and_3_out, and_4_out, and_5_out);

  // Notes on the sheet:
  //   Entrées non utilisées pour l'instant
  //   (Resultat du calcul courant)
  //   (Instruction mettant à jour NZP)
  //   (Instruction courante)
  //   Valeur actuel du registre d'état NZP
  //   (pour l'instant toujours 000)
  //   Test de saut
endmodule

// Off6
module Offset6 (
  input  [15:0] IR,
  output [15:0] Off6
);

  assign Off6 = {{10{IR[5]}}, IR[5:0]};  // Bit_Extender bit_extender_1
endmodule

// Off9
module Offset9 (
  input  [15:0] IR,
  output [15:0] Off9
);

  assign Off9 = {{7{IR[8]}}, IR[8:0]};  // Bit_Extender bit_extender_1
endmodule

module Or16 (
  input  [15:0] in_1,
  output out_2
);

  wire [3:0] or_1_out;

  assign or_1_out = in_1[3:0] | in_1[7:4] | in_1[11:8] | in_1[15:12];  // OR_Gate or_1, 4 bits wide
  or or_2 (out_2, or_1_out[0], or_1_out[1], or_1_out[2], or_1_out[3]);
endmodule

module RamCtrl (
  input  Exec,
  input  Post_Exec,
  input  Fetch,
  input  Post_Fetch,
  input  DoubleIndirection,
  input  Load,
  input  Store,
  output MemLoad,
  output MemStore
);

  wire and_1_out, and_3_out;

  and and_1 (and_1_out, Exec, Load);
  and and_2 (MemStore, Exec, Store);
  and and_3 (and_3_out, Post_Fetch, DoubleIndirection);
  or or_1 (MemLoad, and_3_out, Fetch, and_1_out);
endmodule

module Registres (
  input  [2:0] SR1,
  input  [15:0] IN,
  input  [2:0] SR2,
  input  WriteReg,
  input  WriteR7,
  input  [2:0] DR_SR,
  output [15:0] R0,
  output [15:0] OUT_SR1,
  output [15:0] R1,
  output [15:0] R2,
  output [15:0] R3,
  output [15:0] OUT_SR2,
  output [15:0] R4,
  output [15:0] R5,
  output [15:0] OUT_SR,
  output [15:0] R6,
  output [15:0] R7
);

  wire decoder_1_out0, decoder_1_out1, decoder_1_out2, decoder_1_out3, decoder_1_out4, decoder_1_out5,
       decoder_1_out6, decoder_1_out7;
  wire [2:0] multiplexer_1_out;

  Multiplexer #(.width(3), .enable("false")) multiplexer_1 (
    .in0(DR_SR), .in1(3'b111), .out(multiplexer_1_out), .sel(WriteR7));
  Decoder #(.select(3), .disabled(0)) decoder_1 (
    .out0(decoder_1_out0), .out1(decoder_1_out1), .out2(decoder_1_out2), .out3(decoder_1_out3),
    .out4(decoder_1_out4), .out5(decoder_1_out5), .out6(decoder_1_out6), .out7(decoder_1_out7),
    .sel(multiplexer_1_out), .en(WriteReg));
  Register #(.width(16), .trigger("falling")) u_R0 (.D(IN), .Q(R0), .clk(decoder_1_out0));  // open: en, clr
  Register #(.width(16), .trigger("falling")) u_R1 (.D(IN), .Q(R1), .clk(decoder_1_out1));  // open: en, clr
  Register #(.width(16), .trigger("falling")) u_R2 (.D(IN), .Q(R2), .clk(decoder_1_out2));  // open: en, clr
  Register #(.width(16), .trigger("falling")) u_R3 (.D(IN), .Q(R3), .clk(decoder_1_out3));  // open: en, clr
  Register #(.width(16), .trigger("falling")) u_R4 (.D(IN), .Q(R4), .clk(decoder_1_out4));  // open: en, clr
  Register #(.width(16), .trigger("falling")) u_R5 (.D(IN), .Q(R5), .clk(decoder_1_out5));  // open: en, clr
  Register #(.width(16), .trigger("falling")) u_R6 (.D(IN), .Q(R6), .clk(decoder_1_out6));  // open: en, clr
  Register #(.width(16), .trigger("falling")) u_R7 (.D(IN), .Q(R7), .clk(decoder_1_out7));  // open: en, clr
  Multiplexer #(.select(3), .width(16), .enable("false")) multiplexer_2 (
    .in0(R0), .in1(R1), .in2(R2), .in3(R3), .in4(R4), .in5(R5), .in6(R6), .in7(R7), .out(OUT_SR1), .sel(SR1));
  Multiplexer #(.select(3), .width(16), .enable("false")) multiplexer_3 (
    .in0(R0), .in1(R1), .in2(R2), .in3(R3), .in4(R4), .in5(R5), .in6(R6), .in7(R7), .out(OUT_SR2), .sel(SR2));
  Multiplexer #(.select(3), .width(16), .enable("false")) multiplexer_4 (
    .in0(R0), .in1(R1), .in2(R2), .in3(R3), .in4(R4), .in5(R5), .in6(R6), .in7(R7), .out(OUT_SR), .sel(DR_SR));
endmodule

module RegPC (
  input  Jump,
  input  UseCondition,
  input  [15:0] Result,
  input  TestNZP,
  input  H,
  input  Reset,
  output [15:0] PC
);

  wire and_1_out, and_2_out, and_3_out, or_1_out;
  wire [15:0] adder_1_out, multiplexer_1_out;

  and and_1 (and_1_out, Jump, UseCondition);
  and and_2 (and_2_out, and_1_out, TestNZP);
  and and_3 (and_3_out, Jump, ~UseCondition);  // AND_Gate
  Adder #(.width(16)) adder_1 (.a(PC), .b({16{1'b0}}), .out(adder_1_out), .cin(1'b1));  // open: cout
  or or_1 (or_1_out, and_2_out, and_3_out);
  Multiplexer #(.width(16), .enable("false")) multiplexer_1 (
    .in0(adder_1_out), .in1(Result), .out(multiplexer_1_out), .sel(or_1_out));
  Register #(.width(16), .trigger("falling")) u_PC (.D(multiplexer_1_out), .Q(PC), .clk(H), .clr(Reset));  // open: en
endmodule

module setResetBit (
  input  [15:0] DataIn,
  input  [15:0] NBit,
  input  Mode__0__Reset_1__Set,
  output [15:0] DataOut
);

  wire [15:0] and_1_out, not_1_out, or_1_out, shifter_1_out;

  Shifter #(.width(16)) shifter_1 (.in(16'h1), .\dist (NBit[3:0]), .out(shifter_1_out));
  assign not_1_out = ~shifter_1_out;  // NOT_Gate not_1, 16 bits wide
  assign and_1_out = not_1_out & DataIn;  // AND_Gate and_1, 16 bits wide
  assign or_1_out = shifter_1_out | DataIn;  // OR_Gate or_1, 16 bits wide
  // Probe on or_1_out
  // Probe on and_1_out
  Multiplexer #(.width(16), .enable("false")) multiplexer_1 (
    .in0(and_1_out), .in1(or_1_out), .out(DataOut), .sel(Mode__0__Reset_1__Set));

  // Notes on the sheet:
  //   Calculate bit change
  //   Reset (mask) o= SR1 . not(b)
  //   Set o= SR1+b
endmodule

module SEXTSelector (
  input  [15:0] IR,
  input  [1:0] select,
  output [15:0] Out
);

  wire [15:0] offset6_1_off6, offset9_1_off9, offset11_1_off9;

  Offset11 offset11_1 (.IR(IR), .Off9(offset11_1_off9));
  Offset9 offset9_1 (.IR(IR), .Off9(offset9_1_off9));
  Offset6 offset6_1 (.IR(IR), .Off6(offset6_1_off6));
  Multiplexer #(.select(2), .width(16), .enable("false")) multiplexer_1 (
    .in0(offset11_1_off9), .in1(offset9_1_off9), .in2(offset6_1_off6), .in3({16{1'b0}}), .out(Out),
    .sel(select));
endmodule

// Off11
module Offset11 (
  input  [15:0] IR,
  output [15:0] Off9
);

  assign Off9 = {{5{IR[10]}}, IR[10:0]};  // Bit_Extender bit_extender_1
endmodule

module AddUnit (
  input  [15:0] IR,
  input  [15:0] PC,
  input  [15:0] R,
  output [15:0] Out
);

  wire and_1_out, and_2_out, and_3_out, and_4_out, and_5_out, and_6_out, and_7_out, comparator_1_eq,
       or_1_out, or_2_out, or_3_out;
  wire [1:0] priority_encoder_1_out, priority_encoder_2_out;
  wire [15:0] adder_1_out, multiplexer_1_out, sextselector_1_out;

  Comparator #(.width(5)) comparator_1 (.a(IR[15:11]), .b(5'b01001), .eq(comparator_1_eq));  // open: gt, lt
  // Probe on IR[15]
  // Probe on IR[13]
  // Probe on comparator_1_eq
  // Probe on IR[14]
  // Probe on IR[15:12]
  and and_1 (and_1_out, IR[13], IR[15]);
  and and_2 (and_2_out, ~IR[12], IR[13], IR[15]);  // AND_Gate
  and and_3 (and_3_out, ~IR[13], IR[15]);  // AND_Gate
  and and_4 (and_4_out, IR[14], ~IR[15], ~comparator_1_eq);  // AND_Gate
  and and_5 (and_5_out, IR[12], IR[14], IR[15]);
  // Probe on IR[12]
  or or_1 (or_1_out, ~IR[14], and_1_out);  // OR_Gate
  and and_6 (and_6_out, IR[13], IR[14], ~IR[15]);  // AND_Gate
  and and_7 (and_7_out, ~IR[13], IR[14], ~comparator_1_eq);  // AND_Gate
  or or_2 (or_2_out, ~IR[14], and_2_out, comparator_1_eq);  // OR_Gate
  or or_3 (or_3_out, and_3_out, and_4_out);
  Priority_Encoder #(.select(2)) priority_encoder_1 (
    .in0(comparator_1_eq), .in1(or_1_out), .in2(and_6_out), .in3(and_7_out), .out(priority_encoder_1_out));  // open: gs, en_out, en_in
  // Probe on priority_encoder_1_out
  SEXTSelector sextselector_1 (.IR(IR), .select(priority_encoder_1_out), .Out(sextselector_1_out));
  Adder #(.width(16)) adder_1 (.a(PC), .b({16{1'b0}}), .out(adder_1_out), .cin(1'b1));  // open: cout
  Multiplexer #(.select(2), .width(16), .enable("false")) multiplexer_1 (
    .in0(adder_1_out), .in1(R), .in2({16{1'b0}}), .in3({16{1'b0}}), .out(multiplexer_1_out),
    .sel(priority_encoder_2_out));
  // Probe on priority_encoder_2_out
  Priority_Encoder #(.select(2)) priority_encoder_2 (
    .in0(or_2_out), .in1(or_3_out), .in2(and_5_out), .in3(1'b0), .out(priority_encoder_2_out));  // open: gs, en_out, en_in
  // Probe on sextselector_1_out
  // Probe on multiplexer_1_out
  Adder #(.width(16)) adder_2 (.a(sextselector_1_out), .b(multiplexer_1_out), .out(Out));  // open: cin, cout
  // Probe on Out

  // Notes on the sheet:
  //   PCoffset11= JSR
  //   PCoffset9= /14+13.15
  //   PCoffset6= 13.14./15
  //   0= /13.14./JSR
  //   PC= /14+/12.13.14+JSR
  //   BaseR=/13.15+14./15./JSR
  //   0=12.14.15
  //   00: PC
  //   01: R
  //   1X: 0
endmodule

module WriteSelector (
  input  [15:0] MemOut,
  input  [15:0] AddUnitOut,
  input  [15:0] PC,
  input  [15:0] ALUOut,
  input  LoadMem,
  input  LoadAddUnit,
  input  WriteR7,
  input  Arith,
  output [15:0] Output
);

  wire [1:0] priority_encoder_1_out;
  wire [15:0] adder_1_out;

  Adder #(.width(16)) adder_1 (.a(PC), .b({16{1'b0}}), .out(adder_1_out), .cin(1'b1));  // open: cout
  Priority_Encoder #(.select(2)) priority_encoder_1 (
    .in0(LoadMem), .in1(LoadAddUnit), .in2(WriteR7), .in3(Arith), .out(priority_encoder_1_out));  // open: gs, en_out, en_in
  Multiplexer #(.select(2), .width(16), .enable("false")) multiplexer_1 (
    .in0(MemOut), .in1(AddUnitOut), .in2(adder_1_out), .in3(ALUOut), .out(Output),
    .sel(priority_encoder_1_out));
endmodule
